// Logisim project cdm16_verilog.circ as structural Verilog: 5 circuits, main circuit cdm16
module cdm16 (
  input  [15:0] data_in,
  input  EXC,
  input  [5:0] exc_vec,
  input  IRQ,
  input  [5:0] int_vec,
  input  clock,
  input  hold,
  output [15:0] SP,
  output [15:0] PC,
  output [15:0] PS,
  output [15:0] address,
  output mem,
  output data_ins_prime,
  output [15:0] R0,
  output rd_wr_prime,
  output [15:0] R1,
  output [15:0] R2,
  output word,
  output [15:0] R3,
  output [15:0] data_out,
  output [15:0] R4,
  output [15:0] R5,
  output [15:0] R6,
  output [15:0] FP,
  output [1:0] status,
  output IAck,
  output fetch
);

  wire and_1_out, and_3_out, and_4_out, and_6_out, and_9_out, and_13_out, clk, clk_no_inhibit,
       comparator_1_eq, comparator_3_eq, critical_fault, CUT, d_ff_1_qn, double_fault, exc_latch,
       exc_trig_invalid_inst, exc_trig_pc, exc_trig_sp, exc_triggered, halt, \int , int_en,
       latch_double_fault, latch_int, nor_1_out, not_1_out, not_2_out, not_3_out, or_1_out, or_2_out,
       or_3_out, or_8_out, or_9_out, priority_encoder_1_gs, reset_exc, rti, startup, virtual_instruction,
       \wait ;
  wire [2:0] exc_internal_vec, multiplexer_1_out, phase, priority_encoder_1_out;
  wire [5:0] exc_vec_t;
  wire [9:0] dbg_ucode_addr;
  wire [15:0] bit_extender_1_out, bit_extender_2_out, bit_extender_3_out, bit_extender_4_out,
       bit_extender_5_out, busD, dbg_instruction, fetched_instruction, multiplexer_2_out, multiplexer_3_out,
       multiplexer_4_out, multiplexer_5_out, multiplexer_6_out, or_7_out;
  wire [26:0] dbg_ucommand;
  wire [27:0] multiplexer_8_out, rom_1_data, rom_2_data;

  not not_1 (not_1_out, CUT);
  Register #(.width(6), .trigger("falling")) register_1 (
    .D(exc_vec), .en(EXC), .Q(exc_vec_t), .clk(clk_no_inhibit));  // open: clr
  Counter #(.width(3), .max('h7), .trigger("falling")) counter_1 (
    .load(CUT), .D(3'b000), .count(not_1_out), .Q(phase), .clk(clk));  // open: carry, clr
  nor nor_1 (nor_1_out, phase[0], phase[1], phase[2]);
  D_Flip_Flop #(.trigger("falling")) d_ff_1 (
    .clk(clk), .D(d_ff_1_qn), .Qn(d_ff_1_qn), .en(CUT));  // open: Q, preset, reset
  // verilator_component_1_0_SNAPSHOT_all_cdm16 cdm16_1: pin names not known; wires that end beside it: R0, R1, R2, R3, R4, R5, R6, FP, dbg_instruction, {CUT, dbg_ucommand}, phase, exc_triggered, virtual_instruction, fetch, clock, hold, IRQ, critical_fault, rti, \int , halt, \wait , dbg_ucode_addr
  and and_1 (and_1_out, startup, clk);
  and and_2 (fetch, nor_1_out, d_ff_1_qn);
  or or_1 (or_1_out, or_2_out, EXC);
  or or_2 (or_2_out, exc_trig_invalid_inst, exc_trig_pc, exc_trig_sp);
  D_Flip_Flop #(.trigger("falling")) d_ff_2 (.clk(and_1_out), .D(CUT), .Qn(startup));  // open: Q, preset, en, reset
  and and_3 (and_3_out, or_2_out, EXC);
  Priority_Encoder priority_encoder_1 (
    .in1(exc_trig_sp), .in2(exc_trig_pc), .in3(exc_trig_invalid_inst), .in7(EXC),
    .out(priority_encoder_1_out), .gs(priority_encoder_1_gs));  // open: in0, in4, in5, in6, en_in, en_out
  or or_3 (or_3_out, rti, \int );
  and and_4 (and_4_out, or_1_out, exc_latch);
  or or_4 (latch_double_fault, and_3_out, and_4_out, or_3_out);
  Multiplexer #(.width(3), .enable("false")) multiplexer_1 (
    .in0(priority_encoder_1_out), .in1(3'b100), .out(multiplexer_1_out), .sel(latch_double_fault));
  Comparator #(.width(3), .mode("unsigned")) comparator_1 (
    .a(exc_internal_vec), .b(3'b111), .eq(comparator_1_eq));  // open: gt, lt
  assign bit_extender_1_out = {{13{1'b0}}, exc_internal_vec};  // Bit_Extender bit_extender_1
  assign bit_extender_2_out = {{10{1'b0}}, exc_vec_t};  // Bit_Extender bit_extender_2
  assign bit_extender_3_out = {{10{1'b0}}, exc_vec};  // Bit_Extender bit_extender_3
  assign bit_extender_4_out = {{13{1'b0}}, 3'b100};  // Bit_Extender bit_extender_4
  Register #(.width(3), .trigger("falling")) register_2 (
    .D(multiplexer_1_out), .en(priority_encoder_1_gs), .Q(exc_internal_vec), .clk(clk_no_inhibit));  // open: clr
  Multiplexer #(.width(16), .enable("false")) multiplexer_2 (
    .in0(bit_extender_1_out), .in1(bit_extender_2_out), .out(multiplexer_2_out), .sel(comparator_1_eq));
  Multiplexer #(.width(16), .enable("false")) multiplexer_3 (
    .in0(bit_extender_3_out), .in1(bit_extender_4_out), .out(multiplexer_3_out), .sel(latch_double_fault));
  and and_5 (IAck, fetch, and_6_out);
  and and_6 (and_6_out, IRQ, int_en);
  or or_5 (latch_int, and_6_out, exc_triggered);
  and and_7 (reset_exc, exc_triggered, fetch);
  S_R_Flip_Flop #(.trigger("falling")) s_r_ff_1 (
    .S(priority_encoder_1_gs), .clk(clk_no_inhibit), .R(reset_exc), .Q(exc_latch));  // open: Qn, preset, reset, en
  assign bit_extender_5_out = {{10{1'b0}}, int_vec};  // Bit_Extender bit_extender_5
  Multiplexer #(.width(16), .enable("false")) multiplexer_4 (
    .in0(bit_extender_5_out), .in1(multiplexer_5_out), .out(multiplexer_4_out), .sel(exc_triggered));
  Multiplexer #(.width(16), .enable("false")) multiplexer_5 (
    .in0(multiplexer_2_out), .in1(multiplexer_3_out), .out(multiplexer_5_out), .sel(EXC));
  LED led_1 (.in(clk));
  LED led_2 (.in(int_en));
  and and_8 (critical_fault, double_fault, priority_encoder_1_gs);
  or or_6 (exc_triggered, priority_encoder_1_gs, exc_latch);
  assign or_7_out = multiplexer_4_out | 16'h8000;  // OR_Gate or_7, 16 bits wide
  LED led_3 (.in(clk_no_inhibit));
  Multiplexer #(.width(16), .enable("false")) multiplexer_6 (
    .in0(busD), .in1(or_7_out), .out(multiplexer_6_out), .sel(latch_int));
  Multiplexer #(.width(16), .enable("false")) multiplexer_7 (
    .in0(multiplexer_6_out), .in1(16'h8200), .out(fetched_instruction), .sel(startup));
  not not_2 (not_2_out, fetch);
  or or_8 (or_8_out, latch_int, startup);
  Register #(.width(16), .trigger("falling")) register_3 (
    .D(fetched_instruction), .en(fetch), .Q(dbg_instruction), .clk(clk), .clr(and_9_out));
  and and_9 (and_9_out, fetch, not_2_out);
  D_Flip_Flop #(.trigger("falling")) d_ff_3 (
    .clk(clk), .D(or_8_out), .Q(virtual_instruction), .en(fetch));  // open: Qn, preset, reset
  Comparator #(.width(16), .mode("unsigned")) comparator_2 (
    .a(16'h8004), .b(dbg_instruction), .eq(double_fault));  // open: gt, lt
  Comparator #(.width(28)) comparator_3 (.a({28{1'b0}}), .b(rom_1_data), .eq(comparator_3_eq));  // open: gt, lt
  and and_10 (exc_trig_sp, rom_1_data[25], busD[0]);
  and and_11 (exc_trig_pc, busD[0], rom_1_data[11]);
  and and_12 (exc_trig_invalid_inst, comparator_3_eq, not_3_out);
  not not_3 (not_3_out, exc_latch);
  ROM #(.addrWidth(10), .dataWidth(28)) rom_1 (.addr(dbg_ucode_addr), .data(rom_1_data));  // open: sel
  ROM #(.addrWidth(10), .dataWidth(28)) rom_2 (.addr(dbg_ucode_addr), .data(rom_2_data));  // open: sel
  Multiplexer #(.width(28), .enable("false")) multiplexer_8 (
    .in0(rom_1_data), .in1(rom_2_data), .out(multiplexer_8_out), .sel(exc_triggered));
  Multiplexer #(.width(28), .enable("false")) multiplexer_9 (
    .in0(multiplexer_8_out), .in1(28'h8000000), .out({CUT, dbg_ucommand}), .sel(or_9_out));
  or or_9 (or_9_out, status[1], startup, and_13_out);
  and and_13 (and_13_out, latch_int, fetch);

  // Other names for the same wires on the sheet: address_out[15:0] = address; data = data_ins_prime;
  //   dbg_input_clock = clock; dbg_input_hold = hold; dbg_ucommand[27] = CUT; direct_exc_vec[5:0] = exc_vec;
  //   exc_trig_ext = EXC; pc_value[15:0] = PC; ps_value[15:0] = PS; read = rd_wr_prime; sp_value[15:0] = SP

  // Notes on the sheet:
  //   hold: pull=down
  //   data_in: pull=down
  //   clock: pull=down
  //   IRQ: pull=down
  //   EXC: pull=down
  //   0 - running
  //   1 - waiting
  //   2 - halted
  //   3 - fault
  //   3
  //   2
  //   1
  //   int, reset, rti
  //   Double fault: 1. Unrecoverable instruction
  //   2. Multiple exceptions on the same phase
  //   3. Mutiple exceptions across several phases
  //   contents of rom_1 (hex, n*v repeats v):
  //   4*0 4*c000000 4a00282 5280882 ca00282 d280882 ce00082 e280082 ca01082 d284082 ca20082 d2c0082
  //   c0c0580 4a00282 8440000 a020000 8041000 8024000 8040200 8020800 a210001 5*0 804a001 15*0 c0c8082
  //   80c8082 81c8082 c0c8080 80c8080 81c8080 c028082 8028082 8*0 c0c00ce c0c00ee 80c008e 80c00ae 81c008e
  //   81c00ae c0200ce c0200ee 802008e 80200ae 8040010 8040030 804a009 804a029 800a008 800a028 4a01082
  //   4080888 ca00092 ca000b2 a200049 a200069 4a00282 4a00282 8*0 c0d8082 80d8082 81d8082 c0d8080 80d8080
  //   81d8080 c038082 8038082 8*0 c080980 804a001 801a000 805a001 8000949 8000969 8000400 c080580 16*0
  //   c080980 d284082 9*0 8020800 60*0 4a00282 c084088 4*0 8000949 8000969 120*0 4080888 127*0 c084088
  //   contents of rom_2 (hex, n*v repeats v):
  //   4*8000400 4*c000000 4a00282 5280082 4a00282 5280082 4e00082 4280082 4a01082 5280082 4a20082 5280082
  //   c080580 4a00282 400000 20000 1000 20000 200 20000 210001 5*8000400 8001 15*8000400 c088482 8088482
  //   8188482 c088480 8088480 8188480 c028482 8028482 8*8000400 c0804ce c0804ee 808048e 80804ae 818048e
  //   81804ae c0204ce c0204ee 802048e 80204ae 8000410 8000430 800a409 800a429 8008408 8008428 4a01082
  //   4080088 4a00092 4a000b2 8200449 8200469 4a00282 4a00282 8*8000400 c098482 8098482 8198482 c098480
  //   8098480 8198480 c038482 8038482 8*8000400 c080580 8008401 8018400 8018401 8000549 8000569 8000400
  //   c080180 8*0 8*8000400 4080180 5280082 9000400 8800400 9000400 8000400 9000400 8800400 9000400
  //   8800400 8000400 20000 60*8000400 4a00282 4080088 9000400 9000400 8000400 8000400 149 169 32*8000400
  //   8*0 8*8000400 9000400 800000 9*8000400 9000400 60*8000400 4080088 5*8000400 9000400 9000400
  //   32*8000400 8*0 9*8000400 8800400 70*8000400 4080088 39*8000400 8*0 80*8000400 1000000 39*8000400 8*0
  //   80*8000400 9000400 39*8000400 8*0 120*8000400 8*0 120*8000400
endmodule

module sp_register (
  input  [15:0] In,
  input  clr,
  input  clk,
  input  plus_2,
  input  en,
  input  minus_2,
  output [15:0] Out,
  output [15:0] Mon
);

  wire count, en_t;
  wire [15:0] incdec2_1_out, multiplexer_1_out;

  Multiplexer #(.width(16), .disabled(0), .enable("false")) multiplexer_1 (
    .in0(In), .in1(incdec2_1_out), .out(multiplexer_1_out), .sel(count));
  Register #(.width(16), .trigger("falling")) register_1 (
    .D(multiplexer_1_out), .en(en_t), .Q(Mon), .clk(clk), .clr(clr));
  or or_1 (count, plus_2, minus_2);
  or or_2 (en_t, count, en);
  incdec2 incdec2_1 (.in(Mon), .out(incdec2_1_out), .inc_dec_prime(plus_2));
  Multiplexer #(.width(16), .disabled(0), .enable("false")) multiplexer_2 (
    .in0(Mon), .in1(incdec2_1_out), .out(Out), .sel(minus_2));

  // Notes on the sheet:
  //   en: pull=up
  //   minus_2: pull=down
  //   clk: pull=down
  //   clr: pull=down
  //   plus_2: pull=down
endmodule

module pc_register (
  input  [15:0] In,
  input  clr,
  input  clk,
  input  en,
  input  plus_2,
  input  asrt_inc,
  input  inverse_inc,
  output [15:0] Out,
  output [15:0] Mon
);

  wire en_t, not_1_out;
  wire [15:0] incdec2_1_out, multiplexer_1_out;

  Register #(.width(16), .trigger("falling")) register_1 (
    .D(multiplexer_1_out), .en(en_t), .Q(Mon), .clk(clk), .clr(clr));
  Multiplexer #(.width(16), .disabled(0), .enable("false")) multiplexer_1 (
    .in0(In), .in1(incdec2_1_out), .out(multiplexer_1_out), .sel(plus_2));
  or or_1 (en_t, plus_2, en);
  incdec2 incdec2_1 (.in(Mon), .out(incdec2_1_out), .inc_dec_prime(not_1_out));
  not not_1 (not_1_out, inverse_inc);
  Multiplexer #(.width(16), .disabled(0), .enable("false")) multiplexer_2 (
    .in0(Mon), .in1(incdec2_1_out), .out(Out), .sel(asrt_inc));

  // Other names for the same wires on the sheet: count = plus_2

  // Notes on the sheet:
  //   asrt_inc: pull=down
  //   en: pull=up
  //   inverse_inc: pull=down
  //   clr: pull=down
  //   plus_2: pull=down
  //   clk: pull=down
endmodule

module ps_register (
  input  [3:0] flags,
  input  [15:0] word,
  input  clk,
  input  latch_word,
  input  latch_flags,
  input  ei,
  input  di,
  output [3:0] out_flags,
  output [15:0] out
);

  wire or_1_out, or_3_out, set_int_flag;
  wire [15:0] multiplexer_1_out, multiplexer_2_out;

  Multiplexer #(.width(16), .enable("false")) multiplexer_1 (
    .in0({out[15:4], flags}), .in1({ei, out[14:0]}), .out(multiplexer_1_out), .sel(set_int_flag));
  Multiplexer #(.width(16), .enable("false")) multiplexer_2 (
    .in0(multiplexer_1_out), .in1(word), .out(multiplexer_2_out), .sel(latch_word));
  or or_1 (or_1_out, latch_word, latch_flags);
  or or_2 (set_int_flag, ei, di);
  Register #(.width(16), .trigger("falling")) register_1 (
    .D(multiplexer_2_out), .en(or_3_out), .Q(out), .clk(clk));  // open: clr
  or or_3 (or_3_out, or_1_out, set_int_flag);
  Bit_Extender #(.in_width(16), .out_width(4)) bit_extender_1 (.in(out), .out(out_flags));

  // Notes on the sheet:
  //   flags: pull=down
  //   latch_word: pull=down
  //   di: pull=down
  //   ei: pull=down
  //   clk: pull=down
  //   word: pull=down
  //   latch_flags: pull=down
endmodule

module incdec2 (
  input  [15:0] in,
  input  inc_dec_prime,
  output [15:0] out
);

  wire [15:0] multiplexer_1_out;

  Multiplexer #(.width(16), .enable("false")) multiplexer_1 (
    .in0(16'hfffe), .in1(16'h2), .out(multiplexer_1_out), .sel(inc_dec_prime));
  Adder #(.width(16)) adder_1 (.a(in), .b(multiplexer_1_out), .out(out));  // open: cin, cout

  // Notes on the sheet:
  //   inc_dec_prime: pull=up
endmodule
